// Logisim project AOIS.circ as structural Verilog: 3 circuits, main circuit main
module main (
  input  in_1,
  input  [7:0] in_2,
  output d,
  output d_2,
  output b,
  output b_2,
  output d_3,
  output d_4,
  output b_3,
  output b_4,
  output d_5,
  output d_6,
  output b_5,
  output b_6,
  output d_7,
  output d_8,
  output b_7,
  output b_8
);

  wire and_1_out, and_2_out, and_3_out, and_4_out, and_5_out, and_6_out, and_7_out, and_8_out, and_9_out,
       and_10_out, and_11_out, and_12_out, and_13_out, and_14_out, and_15_out, and_16_out, and_17_out,
       and_18_out, and_19_out, and_20_out, and_21_out, and_22_out, and_23_out, and_24_out, and_25_out,
       and_26_out, and_27_out, and_28_out, and_29_out, and_30_out, and_31_out, and_32_out, and_33_out,
       and_34_out, and_35_out, and_36_out, and_37_out, and_38_out, and_39_out, and_40_out, and_41_out,
       and_42_out, and_43_out, and_44_out, and_45_out, and_46_out, and_47_out, and_48_out, and_49_out,
       and_50_out, and_51_out, and_52_out, and_53_out, and_54_out, and_55_out, and_56_out, not_1_out,
       not_2_out, not_3_out, not_4_out, not_5_out, not_6_out, not_7_out, not_8_out, not_9_out, not_10_out,
       not_11_out, not_12_out, not_13_out, not_14_out, not_15_out, not_16_out, not_17_out, not_18_out,
       not_19_out, not_20_out, not_21_out, not_22_out, not_23_out, not_24_out, not_25_out, not_26_out,
       not_27_out, not_28_out, not_29_out, not_30_out, not_31_out, not_32_out, not_33_out, not_34_out,
       not_35_out, not_36_out, not_37_out, not_38_out, not_39_out, not_40_out, not_41_out, not_42_out,
       not_43_out, not_44_out, not_45_out, not_46_out, not_47_out, not_48_out, not_49_out, not_50_out,
       not_51_out, not_52_out, not_53_out, not_54_out, not_55_out, not_56_out, not_57_out, not_58_out,
       not_59_out, not_60_out, not_61_out, not_62_out, not_63_out, not_64_out;
  wire [7:0] undriven;

  // Probe on undriven
  // Probe on in_2
  not not_1 (not_1_out, in_2[1]);
  not not_2 (not_2_out, undriven[1]);
  not not_3 (not_3_out, in_2[1]);
  not not_4 (not_4_out, b);
  not not_5 (not_5_out, undriven[1]);
  not not_6 (not_6_out, b);
  not not_7 (not_7_out, in_2[1]);
  not not_8 (not_8_out, in_2[1]);
  not not_9 (not_9_out, in_2[0]);
  not not_10 (not_10_out, undriven[0]);
  not not_11 (not_11_out, in_2[0]);
  not not_12 (not_12_out, in_1);
  not not_13 (not_13_out, undriven[0]);
  not not_14 (not_14_out, in_1);
  not not_15 (not_15_out, in_2[0]);
  not not_16 (not_16_out, in_2[0]);
  and and_1 (and_1_out, not_1_out, not_2_out, b);
  and and_2 (and_2_out, not_3_out, undriven[1], not_4_out);
  and and_3 (and_3_out, in_2[1], not_5_out, not_6_out);
  and and_4 (and_4_out, in_2[1], undriven[1], b);
  and and_5 (and_5_out, not_7_out, b);
  and and_6 (and_6_out, not_8_out, undriven[1]);
  and and_7 (and_7_out, undriven[1], b);
  not not_17 (not_17_out, in_2[2]);
  and and_8 (and_8_out, not_17_out, not_18_out, b_3);
  not not_18 (not_18_out, undriven[2]);
  not not_19 (not_19_out, in_2[2]);
  and and_9 (and_9_out, not_19_out, undriven[2], not_20_out);
  not not_20 (not_20_out, b_3);
  not not_21 (not_21_out, undriven[2]);
  and and_10 (and_10_out, in_2[2], not_21_out, not_22_out);
  not not_22 (not_22_out, b_3);
  and and_11 (and_11_out, in_2[2], undriven[2], b_3);
  not not_23 (not_23_out, in_2[2]);
  and and_12 (and_12_out, not_23_out, b_3);
  not not_24 (not_24_out, in_2[2]);
  and and_13 (and_13_out, not_24_out, undriven[2]);
  and and_14 (and_14_out, undriven[2], b_3);
  not not_25 (not_25_out, in_2[3]);
  not not_26 (not_26_out, undriven[3]);
  and and_15 (and_15_out, not_25_out, not_26_out, b_5);
  not not_27 (not_27_out, in_2[3]);
  and and_16 (and_16_out, not_27_out, undriven[3], not_28_out);
  not not_28 (not_28_out, b_5);
  not not_29 (not_29_out, undriven[3]);
  and and_17 (and_17_out, in_2[3], not_29_out, not_30_out);
  not not_30 (not_30_out, b_5);
  and and_18 (and_18_out, in_2[3], undriven[3], b_5);
  not not_31 (not_31_out, in_2[3]);
  and and_19 (and_19_out, not_31_out, b_5);
  not not_32 (not_32_out, in_2[3]);
  and and_20 (and_20_out, not_32_out, undriven[3]);
  and and_21 (and_21_out, undriven[3], b_5);
  and and_22 (and_22_out, not_9_out, not_10_out, in_1);
  and and_23 (and_23_out, not_11_out, undriven[0], not_12_out);
  and and_24 (and_24_out, in_2[0], not_13_out, not_14_out);
  and and_25 (and_25_out, in_2[0], undriven[0], in_1);
  and and_26 (and_26_out, not_15_out, in_1);
  and and_27 (and_27_out, not_16_out, undriven[0]);
  and and_28 (and_28_out, undriven[0], in_1);
  or or_1 (d_3, and_1_out, and_2_out, and_3_out, and_4_out);
  or or_2 (b_3, and_5_out, and_6_out, and_7_out);
  or or_3 (d_5, and_8_out, and_9_out, and_10_out, and_11_out);
  or or_4 (b_5, and_12_out, and_13_out, and_14_out);
  or or_5 (d_7, and_15_out, and_16_out, and_17_out, and_18_out);
  or or_6 (b_7, and_19_out, and_20_out, and_21_out);
  or or_7 (d, and_22_out, and_23_out, and_24_out, and_25_out);
  or or_8 (b, and_26_out, and_27_out, and_28_out);
  not not_33 (not_33_out, in_2[4]);
  not not_34 (not_34_out, undriven[4]);
  not not_35 (not_35_out, in_2[4]);
  not not_36 (not_36_out, b_7);
  not not_37 (not_37_out, undriven[4]);
  not not_38 (not_38_out, b_7);
  not not_39 (not_39_out, in_2[4]);
  not not_40 (not_40_out, in_2[4]);
  not not_41 (not_41_out, in_2[5]);
  not not_42 (not_42_out, undriven[5]);
  not not_43 (not_43_out, in_2[5]);
  not not_44 (not_44_out, b_2);
  not not_45 (not_45_out, undriven[5]);
  not not_46 (not_46_out, b_2);
  not not_47 (not_47_out, in_2[5]);
  not not_48 (not_48_out, in_2[5]);
  not not_49 (not_49_out, in_2[6]);
  not not_50 (not_50_out, undriven[6]);
  not not_51 (not_51_out, in_2[6]);
  not not_52 (not_52_out, b_4);
  not not_53 (not_53_out, undriven[6]);
  not not_54 (not_54_out, b_4);
  not not_55 (not_55_out, in_2[6]);
  not not_56 (not_56_out, in_2[6]);
  not not_57 (not_57_out, in_2[7]);
  not not_58 (not_58_out, undriven[7]);
  not not_59 (not_59_out, in_2[7]);
  not not_60 (not_60_out, b_6);
  not not_61 (not_61_out, undriven[7]);
  not not_62 (not_62_out, b_6);
  not not_63 (not_63_out, in_2[7]);
  not not_64 (not_64_out, in_2[7]);
  and and_29 (and_29_out, not_33_out, not_34_out, b_7);
  and and_30 (and_30_out, not_35_out, undriven[4], not_36_out);
  and and_31 (and_31_out, in_2[4], not_37_out, not_38_out);
  and and_32 (and_32_out, in_2[4], undriven[4], b_7);
  and and_33 (and_33_out, not_39_out, b_7);
  and and_34 (and_34_out, not_40_out, undriven[4]);
  and and_35 (and_35_out, undriven[4], b_7);
  and and_36 (and_36_out, not_41_out, not_42_out, b_2);
  and and_37 (and_37_out, not_43_out, undriven[5], not_44_out);
  and and_38 (and_38_out, in_2[5], not_45_out, not_46_out);
  and and_39 (and_39_out, in_2[5], undriven[5], b_2);
  and and_40 (and_40_out, not_47_out, b_2);
  or or_9 (b_4, and_40_out, and_41_out, and_42_out);
  and and_41 (and_41_out, not_48_out, undriven[5]);
  and and_42 (and_42_out, b_2, b_2);
  and and_43 (and_43_out, not_49_out, not_50_out, b_4);
  and and_44 (and_44_out, not_51_out, undriven[6], not_52_out);
  and and_45 (and_45_out, in_2[6], not_53_out, not_54_out);
  and and_46 (and_46_out, in_2[6], undriven[6], b_4);
  and and_47 (and_47_out, not_55_out, b_4);
  and and_48 (and_48_out, not_56_out, undriven[6]);
  and and_49 (and_49_out, undriven[6], b_4);
  and and_50 (and_50_out, not_57_out, not_58_out, b_6);
  and and_51 (and_51_out, not_59_out, undriven[7], not_60_out);
  and and_52 (and_52_out, in_2[7], not_61_out, not_62_out);
  and and_53 (and_53_out, in_2[7], undriven[7], b_6);
  and and_54 (and_54_out, not_63_out, b_6);
  and and_55 (and_55_out, not_64_out, undriven[7]);
  and and_56 (and_56_out, undriven[7], b_6);
  or or_10 (d_2, and_29_out, and_30_out, and_31_out, and_32_out);
  or or_11 (b_2, and_33_out, and_34_out, and_35_out);
  or or_12 (d_4, and_36_out, and_37_out, and_38_out, and_39_out);
  or or_13 (d_6, and_43_out, and_44_out, and_45_out, and_46_out);
  or or_14 (b_6, and_47_out, and_48_out, and_49_out);
  or or_15 (d_8, and_50_out, and_51_out, and_52_out, and_53_out);
  or or_16 (b_8, and_54_out, and_55_out, and_56_out);
  // Probe on {d_8, d_6, d_4, d_2, d_7, d_5, d_3, d}
  // Probe on {d_8, d_6, d_4, d_2, d_7, d_5, d_3, d}
endmodule

module LR4_1 (
  input  A,
  input  B,
  input  C,
  output d,
  output b_2
);

  wire and_1_out, and_2_out, and_3_out, and_4_out, and_5_out, and_6_out, and_7_out, not_1_out, not_2_out,
       not_3_out, not_4_out, not_5_out, not_6_out, not_7_out, not_8_out;

  not not_1 (not_1_out, A);
  not not_2 (not_2_out, B);
  not not_3 (not_3_out, A);
  not not_4 (not_4_out, C);
  not not_5 (not_5_out, B);
  not not_6 (not_6_out, C);
  not not_7 (not_7_out, A);
  not not_8 (not_8_out, A);
  and and_1 (and_1_out, not_1_out, not_2_out, C);
  and and_2 (and_2_out, not_3_out, B, not_4_out);
  and and_3 (and_3_out, A, not_5_out, not_6_out);
  and and_4 (and_4_out, A, B, C);
  and and_5 (and_5_out, B, C);
  and and_6 (and_6_out, not_7_out, B);
  and and_7 (and_7_out, not_8_out, C);
  or or_1 (d, and_1_out, and_2_out, and_3_out, and_4_out);
  or or_2 (b_2, and_5_out, and_6_out, and_7_out);
endmodule

module LR1_2 (
  input  A,
  input  B,
  input  C,
  input  D,
  output A1,
  output B1,
  output C1,
  output D1
);

  wire and_1_out, and_2_out, and_3_out, and_4_out, and_5_out, and_6_out, not_1_out, not_2_out, not_4_out,
       not_5_out, not_6_out, not_7_out;

  and and_1 (and_1_out, A, not_1_out);
  not not_1 (not_1_out, B);
  not not_2 (not_2_out, A);
  and and_2 (and_2_out, not_2_out, B);
  not not_3 (B1, B);
  not not_4 (not_4_out, B);
  and and_3 (and_3_out, not_4_out, C);
  not not_5 (not_5_out, A);
  and and_4 (and_4_out, not_5_out, C);
  not not_6 (not_6_out, B);
  and and_5 (and_5_out, not_6_out, D);
  not not_7 (not_7_out, A);
  and and_6 (and_6_out, not_7_out, D);
  or or_1 (A1, and_1_out, and_2_out);
  or or_2 (C1, and_3_out, and_4_out);
  or or_3 (D1, and_5_out, and_6_out);
endmodule
