// Logisim project Lab5_var3.circ as structural Verilog: 2 circuits, main circuit main
module main (
  input  v,
  input  Reset,
  output out_3,
  output out_4,
  output q3_prime,
  output out_6,
  output q2_prime,
  output out_8,
  output q1_prime,
  output out_10
);

  wire and_1_out, and_2_out, and_3_out;

  and and_1 (and_1_out, v, q1_prime, q2_prime, q3_prime);
  and and_2 (and_2_out, v, q1_prime, q2_prime);
  and and_3 (and_3_out, v, q1_prime);
  T_flip_flop_with_reset t_flip_flop_with_reset_1 (
    .Increment(and_1_out), .Out(out_3), .Inversed_Out(out_4), .Reset(Reset));
  T_flip_flop_with_reset t_flip_flop_with_reset_2 (
    .Increment(and_2_out), .Out(q3_prime), .Inversed_Out(out_6), .Reset(Reset));
  T_flip_flop_with_reset t_flip_flop_with_reset_3 (
    .Increment(and_3_out), .Out(q2_prime), .Inversed_Out(out_8), .Reset(Reset));
  T_flip_flop_with_reset t_flip_flop_with_reset_4 (.Increment(v), .Out(q1_prime), .Inversed_Out(out_10), .Reset(Reset));
  Hex_Digit_Display hex_digit_display_1 (.value({out_4, out_6, out_8, out_10}));  // open: dp

  // Notes on the sheet:
  //   h1=v
  //   h3
  //   h2
  //   h1
  //   h2=!q1'*v
  //   h3=!q1'*!q2'v
  //   q3
  //   q2
  //   q1
  //   q1=!h1*q1(i-1) + h1*!q1(i-1)
  //   q2=!h2*q2(i-1) + h2*!q2(i-1)
  //   q3=!h3*q3(i-1) + h3*!q3(i-1)
  //   q1'=!h1*q1+h1*!q1
  //   q2'=!h2*q2+h2*!q2
  //   q3'=!h3*q3+h3*!q3
endmodule

module LR5 (
  input  A,
  input  B,
  input  C,
  input  D,
  input  V,
  output h1,
  output h2,
  output h3,
  output h4
);

  wire and_1_out, and_2_out, and_3_out, and_4_out, and_6_out, and_7_out, and_8_out, and_9_out, and_10_out,
       not_1_out, not_2_out, not_3_out, not_4_out, not_5_out, not_6_out, not_7_out, not_8_out, not_9_out,
       not_10_out;

  not not_1 (not_1_out, B);
  not not_2 (not_2_out, C);
  not not_3 (not_3_out, D);
  not not_4 (not_4_out, C);
  not not_5 (not_5_out, D);
  not not_6 (not_6_out, C);
  not not_7 (not_7_out, D);
  not not_8 (not_8_out, D);
  not not_9 (not_9_out, D);
  not not_10 (not_10_out, D);
  and and_1 (and_1_out, A, V);
  and and_2 (and_2_out, B, V);
  and and_3 (and_3_out, C, V);
  and and_4 (and_4_out, D, V);
  and and_5 (h1, A, not_1_out, not_2_out, not_3_out, V);
  and and_6 (and_6_out, A, not_4_out, not_5_out, V);
  and and_7 (and_7_out, B, not_6_out, not_7_out, V);
  and and_8 (and_8_out, C, not_8_out, V);
  and and_9 (and_9_out, B, not_9_out, V);
  and and_10 (and_10_out, A, not_10_out, V);
  or or_1 (h4, and_1_out, and_2_out, and_3_out, and_4_out);
  or or_2 (h2, and_6_out, and_7_out);
  or or_3 (h3, and_8_out, and_9_out, and_10_out);
endmodule
