// Logisim project circuits.circ as structural Verilog: 1 circuit, main circuit T flip flop with reset
module T_flip_flop_with_reset (
  input  Reset,
  input  Increment,
  output Out,
  output Inversed_Out
);

  wire nand_1_out, nand_2_out, nand_3_out, nand_4_out, nand_5_out, nand_6_out, not_1_out, not_2_out, or_1_out;

  or or_1 (or_1_out, Reset, Increment);
  not not_1 (not_1_out, Reset);
  nand nand_1 (nand_1_out, Inversed_Out, or_1_out);
  nand nand_2 (nand_2_out, nand_1_out, or_1_out);
  not not_2 (not_2_out, or_1_out);
  nand nand_3 (nand_3_out, nand_1_out, nand_4_out);
  nand nand_4 (nand_4_out, nand_3_out, nand_2_out);
  nand nand_5 (nand_5_out, nand_3_out, not_2_out);
  nand nand_6 (nand_6_out, not_2_out, nand_4_out);
  nand nand_7 (Out, nand_5_out, not_1_out, Inversed_Out);
  nand nand_8 (Inversed_Out, Out, nand_6_out);

  // Notes on the sheet:
  //   q
endmodule
